# Fritzing sketch ServoClock (saved by Fritzing 0.9.3b)

parts:
  PWM1 = PCA9685 16x12-bit PWM Breakout
  U1 = NodeMCU V1.0
  PWM2 = PCA9685 16x12-bit PWM Breakout
  C1 = Electrolytic Capacitor [capacitance=1000μF voltage=10V package="1010 [SMD, electrolytic]"]
  S1 = Toggle Switch [package=THT]
  J1 = Basic Servo
  J2 = Basic Servo  # not connected
  J3 = Basic Servo  # not connected
  J4 = Basic Servo  # not connected
  J5 = Basic Servo  # not connected
  J6 = Basic Servo  # not connected
  J7 = Basic Servo  # not connected
  J8 = Basic Servo  # not connected
  J9 = Basic Servo  # not connected
  J10 = Basic Servo  # not connected
  J11 = Basic Servo  # not connected
  J12 = Basic Servo  # not connected
  J13 = Basic Servo
  J14 = Basic Servo  # not connected
  J15 = Basic Servo
  J16 = Basic Servo  # not connected
  J17 = Basic Servo
  J18 = Basic Servo  # not connected
  J19 = Basic Servo  # not connected
  J20 = Basic Servo  # not connected
  J21 = Basic Servo  # not connected
  J22 = Basic Servo  # not connected
  J23 = Basic Servo  # not connected
  J24 = Basic Servo  # not connected
  J25 = Basic Servo  # not connected
  J26 = Basic Servo  # not connected
  J27 = Basic Servo  # not connected
  J28 = Basic Servo  # not connected

nets:
  N1: PWM1.no_name_yet#0, J1.pulse
  N2: PWM1.no_name_yet#8, J13.pulse
  VCC: PWM1.no_name_yet#100, PWM1.no_name_yet#108, PWM1.no_name_yet#506, PWM1.no_name_yet#706, U1.Vin, PWM2.no_name_yet#100, PWM2.no_name_yet#108, PWM2.no_name_yet#706, C1.+, S1.L1, J1.vcc, J13.vcc, J15.vcc, J17.vcc
  GND: PWM1.no_name_yet#501, PWM1.no_name_yet#601, PWM1.no_name_yet#701, PWM1.no_name_yet#1000, PWM1.no_name_yet#1008, U1.GND, PWM2.no_name_yet#501, PWM2.no_name_yet#701, PWM2.no_name_yet#1000, PWM2.no_name_yet#1008, C1.-, J1.gnd, J13.gnd, J15.gnd, J17.pulse
  N3: PWM1.no_name_yet#502, PWM1.no_name_yet#602, U1.D3, PWM2.no_name_yet#502
  N4: PWM1.no_name_yet#503, PWM1.no_name_yet#603, U1.D2, PWM2.no_name_yet#503
  N5: PWM1.no_name_yet#504, PWM1.no_name_yet#604, U1.D1, PWM2.no_name_yet#504
  N6: PWM1.no_name_yet#605, PWM2.no_name_yet#505
  N7: U1.3V3, S1.COM
  N8: PWM2.no_name_yet#0, J17.gnd
  N9: PWM2.no_name_yet#8, J15.pulse

notes:
  5V - 3A Input
  Servo 0
  Servo 1
  Servo 2
  Servo 3
  Servo 4
  Servo 5
  Servo 6
  Servo 8
  Servo 9
  Servo 10
  Servo 11
  Servo 12
  Servo 13
  Servo 14
  Attach servos to respective pin
  Programming switch
  1000 uF

custom parts:
  NodeMCU V1.0: ESP8266 based NodeMCU
